# Fritzing sketch breadboard (saved by Fritzing 0.9.1b)
breadboards: 1

parts:
  S1 = Momentary Switch [package=ksa_sealed_tac_switch]
  Raspberry_Pi1 = Raspberry Pi B rev2
  C1 = Capacitor Polarized [package=cpol-radial-100uf-25v]
  S3 = Toggle Switch [package=THT]
  S4 = Pushbutton [package="[THT]"]
  S5 = Pushbutton [package="[THT]"]
  S6 = Pushbutton [package="[THT]"]
  S7 = Pushbutton [package="[THT]"]
  S8 = Pushbutton [package="[THT]"]
  J5 = Basic Servo
  J7 = Basic Servo
  J9 = Basic Servo
  S9 = Momentary Switch [package=ksa_sealed_tac_switch]
  S10 = Momentary Switch [package=ksa_sealed_tac_switch]
  J10 = Basic Servo
  Part1 = Arduino Uno (Rev3)
  J8 = Basic Servo
  LED1 = LED - 5mm [color="Blue (430nm)" package="5 mm [THT]"]
  LED2 = LED - 5mm [color="Blue (430nm)" package="5 mm [THT]"]
  LED3 = LED - 5mm [color="Blue (430nm)" package="5 mm [THT]"]
  C2 = Electrolytic Capacitor [capacitance=47µF package="100 mil [THT, electrolytic]"]
  R3 = Resistor [tolerance=±5% resistance=220 package=THT]
  R4 = Resistor [tolerance=±5% resistance=220 package=THT]
  J6 = Basic Servo

nets:
  GND: S1.2, S4.Pin_1, S4.Pin_2, S5.Pin_1, S5.Pin_2, S6.Pin_1, S6.Pin_2, S7.Pin_1, S7.Pin_2, S8.Pin_1, S8.Pin_2, J5.gnd, J7.gnd, J10.gnd, Part1.GND, C2.-
  N1: S1.3, Part1.D8
  N2: Raspberry_Pi1.5V, LED2.anode
  N3: Raspberry_Pi1.GND, S9.3, S10.3, R3.Pin_1, R4.Pin_1
  N4: Raspberry_Pi1.GPIO_27, LED1.anode
  N5: Raspberry_Pi1.GPIO_22, LED3.anode
  N6: Raspberry_Pi1.GPIO_24, S10.2
  N7: Raspberry_Pi1.GPIO_25, S9.2
  N8: C1.+, S3.L2
  VCC: C1.-, J7.vcc, J10.vcc, Part1.5V, C2.+, J6.vcc
  N9: S3.COM, Part1.RESET
  N10: S4.Pin_3, S4.Pin_4, Part1.D9_PWM
  N11: S5.Pin_3, S5.Pin_4, Part1.D10_PWM/SS
  N12: S6.Pin_3, S6.Pin_4, Part1.D11_PWM/MOSI
  N13: S7.Pin_3, S7.Pin_4, Part1.D12/MISO
  N14: S8.Pin_3, S8.Pin_4, Part1.D13/SCK
  N15: J5.pulse, Part1.D6_PWM
  N16: J7.pulse, Part1.D4
  N17: J9.pulse, Part1.D3_PWM
  N18: J10.pulse, Part1.D7
  N19: Part1.D2, J8.pulse
  N20: Part1.D5_PWM, J6.pulse
  N21: LED1.cathode, LED3.cathode, R4.Pin_0
  N22: LED2.cathode, R3.Pin_0

notes:
  Capacitor prevents uno rebooting on each serial connect in operation mode. Turn switch to off to upload Arduino firmware.
  may need a capacitor for sudden power demand of a starting servo
  LEDs to size, match with correct resistors !
  Serial connection via USB, pi also powers the arduino
  Incoming Power >
